// Logisim project IKEA.circ as structural Verilog: 24 circuits, main circuit main
module main (
  output [7:0] out_1
);

  wire alu_1_itemiszero, alucontrolunit_1_add, alucontrolunit_1_alu_and, alucontrolunit_1_alu_or,
       alucontrolunit_1_donothing, alucontrolunit_1_passnegatedreg1, alucontrolunit_1_passreg1,
       alucontrolunit_1_passreg2, alucontrolunit_1_subtract, controlunit_1_branchx30,
       controlunit_1_condbranch, controlunit_1_enablewrite, controlunit_1_pctox30, controlunit_1_readmemory,
       controlunit_1_uncondbranch, controlunit_1_useimm, controlunit_1_wr_as_rr2, controlunit_1_writememory,
       controlunit_1_writeregalu, controlunit_1_writeregmemory, determinebranch_1_branch, MainClock_out;
  wire [7:0] alu_1_aluoutput, datamemory_1_memoutput, immparser_1_imm, pcc_updater_1_newpc,
       rd2_or_imm_selector_1_value2, registers_1_readdata1, registers_1_readdata2, rr1parser_1_rr1,
       rr2parser_1_rr2, writedataselector_1_writedata, writeregparser_1_writereg;
  wire [63:0] instructionmemory_1_instruction;

  Clock MainClock (.out(MainClock_out));
  DetermineBranch determinebranch_1 (
    .UncondBranch(controlunit_1_uncondbranch), .CondBranch(controlunit_1_condbranch),
    .ItemIsZero(alu_1_itemiszero), .Branch(determinebranch_1_branch));
  DataMemory datamemory_1 (
    .MemAddr(alu_1_aluoutput), .DoMemWrite(controlunit_1_writememory), .DoMemRead(controlunit_1_readmemory),
    .Clock(MainClock_out), .WriteData(registers_1_readdata2), .MemOutput(datamemory_1_memoutput));
  ProgramCounter programcounter_1 (.NewPC(pcc_updater_1_newpc), .ClockTick(MainClock_out), .CurrentPC(out_1));
  ControlUnit controlunit_1 (
    .BinInstruction(instructionmemory_1_instruction), .PCToX30(controlunit_1_pctox30),
    .WR_As_RR2(controlunit_1_wr_as_rr2), .BranchX30(controlunit_1_branchx30),
    .UncondBranch(controlunit_1_uncondbranch), .CondBranch(controlunit_1_condbranch),
    .EnableWrite(controlunit_1_enablewrite), .WriteRegMemory(controlunit_1_writeregmemory),
    .WriteRegALU(controlunit_1_writeregalu), .WriteMemory(controlunit_1_writememory),
    .ReadMemory(controlunit_1_readmemory), .UseImm(controlunit_1_useimm));  // open: SetZero
  RR2Parser rr2parser_1 (
    .WR_As_RR2(controlunit_1_wr_as_rr2), .BinInstruction(instructionmemory_1_instruction),
    .RR2(rr2parser_1_rr2));
  RR1Parser rr1parser_1 (.BinInstruction(instructionmemory_1_instruction), .RR1(rr1parser_1_rr1));
  PCC_Updater pcc_updater_1 (
    .CurrentPC(out_1), .BranchX30(controlunit_1_branchx30), .ReadReg2(registers_1_readdata2),
    .BranchOffset(immparser_1_imm), .Branch(determinebranch_1_branch), .NewPC(pcc_updater_1_newpc));
  WriteDataSelector writedataselector_1 (
    .ALUOutput(alu_1_aluoutput), .WriteRegALU(controlunit_1_writeregalu), .MemOutput(datamemory_1_memoutput),
    .WriteRegMemory(controlunit_1_writeregmemory), .PC(out_1), .PCToX30(controlunit_1_pctox30),
    .WriteData(writedataselector_1_writedata));
  Registers registers_1 (
    .ReadReg1(rr1parser_1_rr1), .WriteData(writedataselector_1_writedata),
    .EnableWrite(controlunit_1_enablewrite), .WriteReg(writeregparser_1_writereg), .Clock(MainClock_out),
    .ReadReg2(rr2parser_1_rr2), .ReadData1(registers_1_readdata1), .ReadData2(registers_1_readdata2));
  WriteRegParser writeregparser_1 (
    .WR_As_RR2(controlunit_1_wr_as_rr2), .BinInstruction(instructionmemory_1_instruction),
    .WriteReg(writeregparser_1_writereg));
  IMMParser immparser_1 (.BinInstruction(instructionmemory_1_instruction), .IMM(immparser_1_imm));
  RD2_Or_Imm_Selector rd2_or_imm_selector_1 (
    .ReadData2(registers_1_readdata2), .IMM(immparser_1_imm), .UseImm(controlunit_1_useimm),
    .Value2(rd2_or_imm_selector_1_value2));
  InstructionMemory instructionmemory_1 (.PC_Address(out_1), .Instruction(instructionmemory_1_instruction));
  ALUControlUnit alucontrolunit_1 (
    .BinInstruction(instructionmemory_1_instruction), .PassNegatedReg1(alucontrolunit_1_passnegatedreg1),
    .PassReg1(alucontrolunit_1_passreg1), .PassReg2(alucontrolunit_1_passreg2),
    .DoNothing(alucontrolunit_1_donothing), .ALU_OR(alucontrolunit_1_alu_or),
    .ALU_And(alucontrolunit_1_alu_and), .Subtract(alucontrolunit_1_subtract), .Add(alucontrolunit_1_add));
  ALU alu_1 (
    .Add(alucontrolunit_1_add), .Value1(registers_1_readdata1), .Subtract(alucontrolunit_1_subtract),
    .Value2(rd2_or_imm_selector_1_value2), .ALU_And(alucontrolunit_1_alu_and),
    .ALU_Or(alucontrolunit_1_alu_or), .DoNothing(alucontrolunit_1_donothing),
    .PassReg2(alucontrolunit_1_passreg2), .PassReg1(alucontrolunit_1_passreg1),
    .PassNegatedReg1(alucontrolunit_1_passnegatedreg1), .ALUOutput(alu_1_aluoutput),
    .ItemIsZero(alu_1_itemiszero));

  // Notes on the sheet:
  //   Step 2: ID
  //   Justin Chen
  //   CPU Name: IKEA
  //   Step 4: ME
  //   Step 5: WB
  //   Step 1: IF
  //   I pledge my honor that I have abided by the Stevens Honor System.
  //   Step 3: EX
endmodule

module Registers (
  input  [7:0] ReadReg1,
  input  [7:0] WriteData,
  input  EnableWrite,
  input  [7:0] WriteReg,
  input  Clock,
  input  [7:0] ReadReg2,
  output [7:0] ReadData1,
  output [7:0] ReadData2
);

  wire and_1_out, and_2_out, and_3_out, and_4_out, and_5_out, and_6_out, and_7_out, and_8_out, and_9_out,
       and_10_out, and_11_out, and_12_out, and_13_out, and_14_out, and_15_out, and_16_out, and_17_out,
       and_18_out, and_19_out, and_20_out, and_21_out, and_22_out, and_23_out, and_24_out, and_25_out,
       and_26_out, and_27_out, and_28_out, and_29_out, and_30_out, and_31_out, decoder_1_out0,
       decoder_1_out1, decoder_1_out2, decoder_1_out3, decoder_1_out4, decoder_1_out5, decoder_1_out6,
       decoder_1_out7, decoder_1_out8, decoder_1_out9, decoder_1_out10, decoder_1_out11, decoder_1_out12,
       decoder_1_out13, decoder_1_out14, decoder_1_out15, decoder_1_out16, decoder_1_out17, decoder_1_out18,
       decoder_1_out19, decoder_1_out20, decoder_1_out21, decoder_1_out22, decoder_1_out23, decoder_1_out24,
       decoder_1_out25, decoder_1_out26, decoder_1_out27, decoder_1_out28, decoder_1_out29, decoder_1_out30,
       decoder_1_out31;
  wire [4:0] fivebitselector_1_last5, fivebitselector_2_last5, fivebitselector_3_last5;
  wire [7:0] register_1_q, register_2_q, register_3_q, register_4_q, register_5_q, register_6_q,
       register_7_q, register_8_q, register_9_q, register_10_q, register_11_q, register_12_q, register_13_q,
       register_14_q, register_15_q, register_16_q, register_17_q, register_18_q, register_19_q,
       register_20_q, register_21_q, register_22_q, register_23_q, register_24_q, register_25_q,
       register_26_q, register_27_q, register_28_q, register_29_q, register_31_q, register_32_q;

  FiveBitSelector fivebitselector_1 (.EightBit(WriteReg), .Last5(fivebitselector_1_last5));
  Decoder #(.select(5)) decoder_1 (
    .out0(decoder_1_out0), .out1(decoder_1_out1), .out2(decoder_1_out2), .out3(decoder_1_out3),
    .out4(decoder_1_out4), .out5(decoder_1_out5), .out6(decoder_1_out6), .out7(decoder_1_out7),
    .out8(decoder_1_out8), .out9(decoder_1_out9), .out10(decoder_1_out10), .out11(decoder_1_out11),
    .out12(decoder_1_out12), .out13(decoder_1_out13), .out14(decoder_1_out14), .out15(decoder_1_out15),
    .out16(decoder_1_out16), .out17(decoder_1_out17), .out18(decoder_1_out18), .out19(decoder_1_out19),
    .out20(decoder_1_out20), .out21(decoder_1_out21), .out22(decoder_1_out22), .out23(decoder_1_out23),
    .out24(decoder_1_out24), .out25(decoder_1_out25), .out26(decoder_1_out26), .out27(decoder_1_out27),
    .out28(decoder_1_out28), .out29(decoder_1_out29), .out30(decoder_1_out30), .out31(decoder_1_out31),
    .sel(fivebitselector_1_last5));  // open: en
  and and_1 (and_1_out, decoder_1_out0, EnableWrite);
  and and_2 (and_2_out, decoder_1_out1, EnableWrite);
  and and_3 (and_3_out, decoder_1_out2, EnableWrite);
  and and_4 (and_4_out, decoder_1_out3, EnableWrite);
  and and_5 (and_5_out, decoder_1_out4, EnableWrite);
  and and_6 (and_6_out, decoder_1_out5, EnableWrite);
  and and_7 (and_7_out, decoder_1_out6, EnableWrite);
  and and_8 (and_8_out, decoder_1_out7, EnableWrite);
  Register register_1 (.D(WriteData), .en(and_1_out), .clk(Clock), .Q(register_1_q));  // open: clr
  Register register_2 (.D(WriteData), .en(and_2_out), .clk(Clock), .Q(register_2_q));  // open: clr
  Register register_3 (.D(WriteData), .en(and_3_out), .clk(Clock), .Q(register_3_q));  // open: clr
  Register register_4 (.D(WriteData), .en(and_4_out), .clk(Clock), .Q(register_4_q));  // open: clr
  Register register_5 (.D(WriteData), .en(and_5_out), .clk(Clock), .Q(register_5_q));  // open: clr
  Register register_6 (.D(WriteData), .en(and_6_out), .clk(Clock), .Q(register_6_q));  // open: clr
  Register register_7 (.D(WriteData), .en(and_7_out), .clk(Clock), .Q(register_7_q));  // open: clr
  Register register_8 (.D(WriteData), .en(and_8_out), .clk(Clock), .Q(register_8_q));  // open: clr
  Register register_9 (.D(WriteData), .en(and_9_out), .clk(Clock), .Q(register_9_q));  // open: clr
  and and_9 (and_9_out, decoder_1_out8, EnableWrite);
  Register register_10 (.D(WriteData), .en(and_10_out), .clk(Clock), .Q(register_10_q));  // open: clr
  and and_10 (and_10_out, decoder_1_out9, EnableWrite);
  Register register_11 (.D(WriteData), .en(and_11_out), .clk(Clock), .Q(register_11_q));  // open: clr
  and and_11 (and_11_out, decoder_1_out10, EnableWrite);
  Register register_12 (.D(WriteData), .en(and_12_out), .clk(Clock), .Q(register_12_q));  // open: clr
  and and_12 (and_12_out, decoder_1_out11, EnableWrite);
  Register register_13 (.D(WriteData), .en(and_13_out), .clk(Clock), .Q(register_13_q));  // open: clr
  and and_13 (and_13_out, decoder_1_out12, EnableWrite);
  Register register_14 (.D(WriteData), .en(and_14_out), .clk(Clock), .Q(register_14_q));  // open: clr
  and and_14 (and_14_out, decoder_1_out13, EnableWrite);
  Register register_15 (.D(WriteData), .en(and_15_out), .clk(Clock), .Q(register_15_q));  // open: clr
  and and_15 (and_15_out, decoder_1_out14, EnableWrite);
  Register register_16 (.D(WriteData), .en(and_16_out), .clk(Clock), .Q(register_16_q));  // open: clr
  and and_16 (and_16_out, decoder_1_out15, EnableWrite);
  Register register_17 (.D(WriteData), .en(and_17_out), .clk(Clock), .Q(register_17_q));  // open: clr
  and and_17 (and_17_out, decoder_1_out16, EnableWrite);
  Register register_18 (.D(WriteData), .en(and_18_out), .clk(Clock), .Q(register_18_q));  // open: clr
  and and_18 (and_18_out, decoder_1_out17, EnableWrite);
  Register register_19 (.D(WriteData), .en(and_19_out), .clk(Clock), .Q(register_19_q));  // open: clr
  and and_19 (and_19_out, decoder_1_out18, EnableWrite);
  Register register_20 (.D(WriteData), .en(and_20_out), .clk(Clock), .Q(register_20_q));  // open: clr
  and and_20 (and_20_out, decoder_1_out19, EnableWrite);
  Register register_21 (.D(WriteData), .en(and_21_out), .clk(Clock), .Q(register_21_q));  // open: clr
  and and_21 (and_21_out, decoder_1_out20, EnableWrite);
  Register register_22 (.D(WriteData), .en(and_22_out), .clk(Clock), .Q(register_22_q));  // open: clr
  and and_22 (and_22_out, decoder_1_out21, EnableWrite);
  Register register_23 (.D(WriteData), .en(and_23_out), .clk(Clock), .Q(register_23_q));  // open: clr
  and and_23 (and_23_out, decoder_1_out22, EnableWrite);
  Register register_24 (.D(WriteData), .en(and_24_out), .clk(Clock), .Q(register_24_q));  // open: clr
  and and_24 (and_24_out, decoder_1_out23, EnableWrite);
  Register register_25 (.D(WriteData), .en(and_25_out), .clk(Clock), .Q(register_25_q));  // open: clr
  and and_25 (and_25_out, decoder_1_out24, EnableWrite);
  Register register_26 (.D(WriteData), .en(and_26_out), .clk(Clock), .Q(register_26_q));  // open: clr
  and and_26 (and_26_out, decoder_1_out25, EnableWrite);
  Register register_27 (.D(WriteData), .en(and_27_out), .clk(Clock), .Q(register_27_q));  // open: clr
  and and_27 (and_27_out, decoder_1_out26, EnableWrite);
  Register register_28 (.D(WriteData), .en(and_28_out), .clk(Clock), .Q(register_28_q));  // open: clr
  and and_28 (and_28_out, decoder_1_out27, EnableWrite);
  Register register_29 (.D(WriteData), .en(and_29_out), .clk(Clock), .Q(register_29_q));  // open: clr
  and and_29 (and_29_out, decoder_1_out28, EnableWrite);
  Register register_30 (.D(WriteData), .en(and_30_out), .clk(Clock), .Q(register_26_q));  // open: clr
  and and_30 (and_30_out, decoder_1_out29, EnableWrite);
  Register register_31 (.D(WriteData), .en(and_31_out), .clk(Clock), .Q(register_31_q));  // open: clr
  and and_31 (and_31_out, decoder_1_out30, EnableWrite);
  Register register_32 (.D({8{1'b0}}), .en(1'b0), .clk(Clock), .Q(register_32_q));  // open: clr
  Multiplexer #(.select(5), .width(8)) multiplexer_1 (
    .in0(register_1_q), .in1(register_2_q), .in2(register_3_q), .in3(register_4_q), .in4(register_5_q),
    .in5(register_6_q), .in6(register_7_q), .in7(register_8_q), .in8(register_9_q), .in9(register_10_q),
    .in10(register_11_q), .in11(register_12_q), .in12(register_13_q), .in13(register_14_q),
    .in14(register_15_q), .in15(register_16_q), .in16(register_17_q), .in17(register_18_q),
    .in18(register_19_q), .in19(register_20_q), .in20(register_21_q), .in21(register_22_q),
    .in22(register_23_q), .in23(register_24_q), .in24(register_25_q), .in25(register_26_q),
    .in26(register_27_q), .in27(register_28_q), .in28(register_29_q), .in29(register_26_q),
    .in30(register_31_q), .in31(register_32_q), .out(ReadData1), .sel(fivebitselector_2_last5));
  Multiplexer #(.select(5), .width(8)) multiplexer_2 (
    .in0(register_1_q), .in1(register_2_q), .in2(register_3_q), .in3(register_4_q), .in4(register_5_q),
    .in5(register_6_q), .in6(register_7_q), .in7(register_8_q), .in8(register_9_q), .in9(register_10_q),
    .in10(register_11_q), .in11(register_12_q), .in12(register_13_q), .in13(register_14_q),
    .in14(register_15_q), .in15(register_16_q), .in16(register_17_q), .in17(register_18_q),
    .in18(register_19_q), .in19(register_20_q), .in20(register_21_q), .in21(register_22_q),
    .in22(register_23_q), .in23(register_24_q), .in24(register_25_q), .in25(register_26_q),
    .in26(register_27_q), .in27(register_28_q), .in28(register_29_q), .in29(register_26_q),
    .in30(register_31_q), .in31(register_32_q), .out(ReadData2), .sel(fivebitselector_3_last5));
  FiveBitSelector fivebitselector_2 (.EightBit(ReadReg1), .Last5(fivebitselector_2_last5));
  FiveBitSelector fivebitselector_3 (.EightBit(ReadReg2), .Last5(fivebitselector_3_last5));

  // Notes on the sheet:
  //   NOT enable write!
  //   Memory to write to
  //   XZR/X31
endmodule

module FiveBitSelector (
  input  [7:0] EightBit,
  output [4:0] Last5
);


  assign Last5 = EightBit[4:0];
endmodule

module OneBitAdder (
  input  InputA,
  input  InputB,
  input  Cin,
  output Sum,
  output Carry
);

  wire and_1_out, and_2_out, and_3_out, xor_1_out;

  and and_1 (and_1_out, InputA, InputB);
  and and_2 (and_2_out, InputA, Cin);
  and and_3 (and_3_out, InputB, Cin);
  xor xor_1 (xor_1_out, InputA, InputB);
  xor xor_2 (Sum, Cin, xor_1_out);
  or or_1 (Carry, and_1_out, and_2_out, and_3_out);
endmodule

module EightBitAdder (
  input  Cin,
  input  [7:0] InputA,
  input  [7:0] InputB,
  output [7:0] Sum,
  output Carry
);

  wire onebitadder_1_carry, onebitadder_2_carry, onebitadder_3_carry, onebitadder_4_carry,
       onebitadder_5_carry, onebitadder_6_carry, onebitadder_7_carry;

  OneBitAdder onebitadder_1 (
    .InputA(InputA[0]), .InputB(InputB[0]), .Cin(Cin), .Sum(Sum[0]), .Carry(onebitadder_1_carry));
  OneBitAdder onebitadder_2 (
    .InputA(InputA[1]), .InputB(InputB[1]), .Cin(onebitadder_1_carry), .Sum(Sum[1]),
    .Carry(onebitadder_2_carry));
  OneBitAdder onebitadder_3 (
    .InputA(InputA[2]), .InputB(InputB[2]), .Cin(onebitadder_2_carry), .Sum(Sum[2]),
    .Carry(onebitadder_3_carry));
  OneBitAdder onebitadder_4 (
    .InputA(InputA[3]), .InputB(InputB[3]), .Cin(onebitadder_3_carry), .Sum(Sum[3]),
    .Carry(onebitadder_4_carry));
  OneBitAdder onebitadder_5 (
    .InputA(InputA[4]), .InputB(InputB[4]), .Cin(onebitadder_4_carry), .Sum(Sum[4]),
    .Carry(onebitadder_5_carry));
  OneBitAdder onebitadder_6 (
    .InputA(InputA[5]), .InputB(InputB[5]), .Cin(onebitadder_5_carry), .Sum(Sum[5]),
    .Carry(onebitadder_6_carry));
  OneBitAdder onebitadder_7 (
    .InputA(InputA[6]), .InputB(InputB[6]), .Cin(onebitadder_6_carry), .Sum(Sum[6]),
    .Carry(onebitadder_7_carry));
  OneBitAdder onebitadder_8 (
    .InputA(InputA[7]), .InputB(InputB[7]), .Cin(onebitadder_7_carry), .Sum(Sum[7]), .Carry(Carry));

  // Notes on the sheet:
  //   LSB
  //   MSB
endmodule

module EightBitTwosComplement (
  input  [7:0] PositiveBinary,
  output [7:0] NegativeBinary
);

  wire [7:0] not_1_out;

  not not_1 (not_1_out[0], PositiveBinary[0]);
  not not_2 (not_1_out[1], PositiveBinary[1]);
  not not_3 (not_1_out[2], PositiveBinary[2]);
  not not_4 (not_1_out[3], PositiveBinary[3]);
  not not_5 (not_1_out[4], PositiveBinary[4]);
  not not_6 (not_1_out[5], PositiveBinary[5]);
  not not_7 (not_1_out[6], PositiveBinary[6]);
  not not_8 (not_1_out[7], PositiveBinary[7]);
  EightBitAdder eightbitadder_1 (.Cin(1'b0), .InputA(not_1_out), .InputB(8'h1), .Sum(NegativeBinary));  // open: Carry
endmodule

module EightBitSubtractor (
  input  [7:0] InputA,
  input  [7:0] InputB,
  output [7:0] Difference
);

  wire [7:0] eightbittwoscomplement_1_negativebinary;

  EightBitTwosComplement eightbittwoscomplement_1 (
    .PositiveBinary(InputB), .NegativeBinary(eightbittwoscomplement_1_negativebinary));
  EightBitAdder eightbitadder_1 (
    .Cin(1'b0), .InputA(InputA), .InputB(eightbittwoscomplement_1_negativebinary), .Sum(Difference));  // open: Carry
endmodule

module ControlUnit (
  input  [63:0] BinInstruction,
  output PCToX30,
  output WR_As_RR2,
  output BranchX30,
  output UncondBranch,
  output CondBranch,
  output EnableWrite,
  output WriteRegMemory,
  output WriteRegALU,
  output WriteMemory,
  output ReadMemory,
  output UseImm,
  output SetZero
);

  or or_1 (EnableWrite, BinInstruction[58], BinInstruction[59]);

  assign BranchX30 = BinInstruction[55];
  assign CondBranch = BinInstruction[57];
  assign PCToX30 = BinInstruction[53];
  assign ReadMemory = BinInstruction[61];
  assign SetZero = BinInstruction[63];
  assign UncondBranch = BinInstruction[56];
  assign UseImm = BinInstruction[62];
  assign WR_As_RR2 = BinInstruction[54];
  assign WriteMemory = BinInstruction[60];
  assign WriteRegALU = BinInstruction[59];
  assign WriteRegMemory = BinInstruction[58];

  // Notes on the sheet:
  //   LSB
  //   MSB
  //   Control Units work from 63-48
  //   EnableWrite will determine if we write registers at all
endmodule

module ALUControlUnit (
  input  [63:0] BinInstruction,
  output PassNegatedReg1,
  output PassReg1,
  output PassReg2,
  output DoNothing,
  output ALU_OR,
  output ALU_And,
  output Subtract,
  output Add
);


  assign Add = BinInstruction[47];
  assign ALU_And = BinInstruction[45];
  assign ALU_OR = BinInstruction[44];
  assign DoNothing = BinInstruction[43];
  assign PassNegatedReg1 = BinInstruction[40];
  assign PassReg1 = BinInstruction[41];
  assign PassReg2 = BinInstruction[42];
  assign Subtract = BinInstruction[46];

  // Notes on the sheet:
  //   ALU Control Unit works from 47-40
endmodule

module PCC_Updater (
  input  [7:0] CurrentPC,
  input  BranchX30,
  input  [7:0] ReadReg2,
  input  [7:0] BranchOffset,
  input  Branch,
  output [7:0] NewPC
);

  wire eightbitadder_1_carry;
  wire [7:0] eightbitadder_1_sum, eightbitadder_2_sum, eightbitadder_3_sum, eightbitadder_4_sum,
       multiplexer_1_out, multiplexer_2_out;

  EightBitAdder eightbitadder_1 (
    .Cin(1'b0), .InputA(8'h8), .InputB(CurrentPC), .Sum(eightbitadder_1_sum), .Carry(eightbitadder_1_carry));
  EightBitAdder eightbitadder_2 (
    .Cin(1'b0), .InputA(CurrentPC), .InputB(BranchOffset), .Sum(eightbitadder_2_sum));  // open: Carry
  Multiplexer #(.width(8)) multiplexer_1 (
    .in0(eightbitadder_1_sum), .in1(CurrentPC), .out(multiplexer_1_out), .sel(eightbitadder_1_carry));
  EightBitAdder eightbitadder_3 (
    .Cin(1'b0), .InputA(8'h2), .InputB({8{1'b1}}), .Sum(eightbitadder_3_sum));  // open: Carry
  EightBitAdder eightbitadder_4 (
    .Cin(1'b0), .InputA({8{1'b1}}), .InputB(8'h2), .Sum(eightbitadder_4_sum));  // open: Carry
  Multiplexer #(.width(8)) multiplexer_2 (
    .in0(multiplexer_1_out), .in1(ReadReg2), .out(multiplexer_2_out), .sel(BranchX30));
  Multiplexer #(.width(8)) multiplexer_3 (
    .in0(multiplexer_2_out), .in1(eightbitadder_2_sum), .out(NewPC), .sel(Branch));

  // Notes on the sheet:
  //   If we branch, we will need to take into account the branching label
  //   For example:
  //   2 - 00000010
  //   1 - 00000001
  //   -2 - 11111110
  //    This is truncated, but we're fine->
  //   memory calculations can never be negative
  //   We may end up doing subtraction on two unsigned integers.
  //   Let's say we are at address 2 and want to offset address 1
  //   255 - 11111111
  //   -255 - 00000001
  //   1 - 0000001
  //   However, this works exactly like signed subtraction. We won't get an underflow since
  //   If we're still wonky about this, let's try an extreme case. Going from location 255 to location 1
  //   Return
  //   Branching
  //   The assembler would do:
  //   1 - 2
  //   00000001 + 11111110 = 11111111
  //   Because when it's time to calculate the offset, PCC_Updater here will take instruction location 2, and add the offset (-1)
  //   Now in PCC Updater
  //   We want to go from 255 to 1. Take 255 and add this offset
  //   Turns out that overflow we truncated didn't matter since we never ended up using it.
  //   you handle negative numbers (which doesn't exist here)
  //   Assembler Offset Calculation
  //   Lesson of the day: Unsigned and Signed subtraction are exactly the same - the only difference is how
  //   Choose X30 if true
  //   PC+8
  //   1 - 255 = 00000010
  //   If we have overflow, use currentPC
  //   <--- Now, this is -1. BUT THAT'S FINE!
  //   If you look at the sum here,
  //   it's 00000001
  //   It's a positive number again!
  //   If you look at the sum here, it's 000000001
  //   It's still a positive number!
  //   Choose branch if true
endmodule

module InstructionMemory (
  input  [7:0] PC_Address,
  output [63:0] Instruction
);

  // ROM #(.line("octo")) rom_1: pin names not known; wires that end beside it: PC_Address, Instruction[7:0], Instruction[15:8], Instruction[23:16], Instruction[31:24], Instruction[39:32], Instruction[47:40], Instruction[55:48], Instruction[63:56]

  // Notes on the sheet:
  //   Bottom of Mem (LSB)
  //   "Top" of Mem (MSB)
  //   contents of rom_1 (hex, n*v repeats v):
  //   0 0 0 1 0 4 0 48 1 0 1 1 0 4 0 48 2 0 0 0 2 80 0 64 3 1 0 0 2 80 0 64 4 3 2 0 20 40 0 8 0 4 18 8 0 2
  //   0 42 4 0 0 0 1 80 40 50 0 0 18 20 0 8 0 41 5 3 2 0 80 80 0 8 5 0 0 0 1 80 40 50 6 0 8 40 0 4 0 48
  //   Each Instruction in IKEA is 8 bytes - when instructions are fetched, we return all 8 bytes of the instruction
endmodule

module DataMemory (
  input  [7:0] MemAddr,
  input  DoMemWrite,
  input  DoMemRead,
  input  Clock,
  input  [7:0] WriteData,
  output [7:0] MemOutput
);

  RAM #(.asyncread("true")) ram_1 (
    .addr(MemAddr), .we(DoMemWrite), .oe(DoMemRead), .clk(Clock), .din(WriteData), .dout(MemOutput));

  // Notes on the sheet:
  //   This writes data one byte and a time (and reads one byte at a time)
  //   I don't know why RAM defaults to reading synchronously, but IRL, reading is combinational
  //   MUCHO IMPORTANTE!!!!
  //   TURN ON ASYNCHRONOUS READ!!!
endmodule

module RR1Parser (
  input  [63:0] BinInstruction,
  output [7:0] RR1
);


  assign RR1 = BinInstruction[15:8];

  // Notes on the sheet:
  //   LSB
  //   MSB
  //   From 15-8
endmodule

module RR2Parser (
  input  WR_As_RR2,
  input  [63:0] BinInstruction,
  output [7:0] RR2
);

  Multiplexer #(.width(8)) multiplexer_1 (
    .in0(BinInstruction[23:16]), .in1(BinInstruction[7:0]), .out(RR2), .sel(WR_As_RR2));

  // Notes on the sheet:
  //   LSB
  //   MSB
  //   Usually, it's from 23-16
  //   But if WR is RR2, read from 7-0
  //   It depends on WR_As_RR2 flag
endmodule

module ALU (
  input  Add,
  input  [7:0] Value1,
  input  Subtract,
  input  [7:0] Value2,
  input  ALU_And,
  input  ALU_Or,
  input  DoNothing,
  input  PassReg2,
  input  PassReg1,
  input  PassNegatedReg1,
  output [7:0] ALUOutput,
  output ItemIsZero
);

  wire [7:0] eightbitadder_1_sum, eightbitand_1_andoutput, eightbitor_1_oroutput,
       eightbitsubtractor_1_difference, multiplexer_1_out, multiplexer_2_out, multiplexer_3_out,
       multiplexer_4_out, multiplexer_5_out, multiplexer_6_out, multiplexer_7_out, not_1_out;

  EightBitAdder eightbitadder_1 (
    .Cin(1'b0), .InputA(Value1), .InputB(Value2), .Sum(eightbitadder_1_sum));  // open: Carry
  EightBitSubtractor eightbitsubtractor_1 (
    .InputA(Value1), .InputB(Value2), .Difference(eightbitsubtractor_1_difference));
  EightBitAnd eightbitand_1 (.InputA(Value1), .InputB(Value2), .ANDOutput(eightbitand_1_andoutput));
  EightBitOr eightbitor_1 (.InputA(Value1), .InputB(Value2), .OROutput(eightbitor_1_oroutput));
  Multiplexer #(.width(8)) multiplexer_1 (
    .in0({8{1'b0}}), .in1(eightbitadder_1_sum), .out(multiplexer_1_out), .sel(Add));
  Multiplexer #(.width(8)) multiplexer_2 (
    .in0(multiplexer_1_out), .in1(eightbitsubtractor_1_difference), .out(multiplexer_2_out), .sel(Subtract));
  Multiplexer #(.width(8)) multiplexer_3 (
    .in0(multiplexer_2_out), .in1(eightbitand_1_andoutput), .out(multiplexer_3_out), .sel(ALU_And));
  Multiplexer #(.width(8)) multiplexer_4 (
    .in0(multiplexer_3_out), .in1(eightbitor_1_oroutput), .out(multiplexer_4_out), .sel(ALU_Or));
  Multiplexer #(.width(8)) multiplexer_5 (
    .in0(multiplexer_4_out), .in1({8{1'b0}}), .out(multiplexer_5_out), .sel(DoNothing));
  Multiplexer #(.width(8)) multiplexer_6 (
    .in0(multiplexer_5_out), .in1(Value2), .out(multiplexer_6_out), .sel(PassReg2));
  Multiplexer #(.width(8)) multiplexer_7 (
    .in0(multiplexer_6_out), .in1(Value1), .out(multiplexer_7_out), .sel(PassReg1));
  assign not_1_out = ~Value1;  // NOT_Gate not_1, 8 bits wide
  Multiplexer #(.width(8)) multiplexer_8 (
    .in0(multiplexer_7_out), .in1(not_1_out), .out(ALUOutput), .sel(PassNegatedReg1));
  EightBitZeroChecker eightbitzerochecker_1 (.CheckInput(ALUOutput), .IsAllZero(ItemIsZero));

  // Notes on the sheet:
  //   Add if add flag is true
  //   Subtract if sub flag is true
  //   AND if and flag is true
  //   OR if or flag is true
  //   Pass 0 if doNothing is true
  //   Just pass Reg2 is that's true
  //   Pass Reg1 if that's true
  //   Pass Negated Reg 1 if it's true
  //   We should also output if the ALU returned 0
endmodule

module EightBitAnd (
  input  [7:0] InputA,
  input  [7:0] InputB,
  output [7:0] ANDOutput
);

  and and_1 (ANDOutput[0], InputA[0], InputB[0]);
  and and_2 (ANDOutput[1], InputA[1], InputB[1]);
  and and_3 (ANDOutput[2], InputA[2], InputB[2]);
  and and_4 (ANDOutput[3], InputA[3], InputB[3]);
  and and_5 (ANDOutput[4], InputA[4], InputB[4]);
  and and_6 (ANDOutput[5], InputA[5], InputB[5]);
  and and_7 (ANDOutput[6], InputA[6], InputB[6]);
  and and_8 (ANDOutput[7], InputA[7], InputB[7]);
endmodule

module EightBitOr (
  input  [7:0] InputA,
  input  [7:0] InputB,
  output [7:0] OROutput
);

  or or_1 (OROutput[0], InputA[0], InputB[0]);
  or or_2 (OROutput[1], InputA[1], InputB[1]);
  or or_3 (OROutput[2], InputA[2], InputB[2]);
  or or_4 (OROutput[3], InputA[3], InputB[3]);
  or or_5 (OROutput[4], InputA[4], InputB[4]);
  or or_6 (OROutput[5], InputA[5], InputB[5]);
  or or_7 (OROutput[6], InputA[6], InputB[6]);
  or or_8 (OROutput[7], InputA[7], InputB[7]);
endmodule

module DetermineBranch (
  input  UncondBranch,
  input  CondBranch,
  input  ItemIsZero,
  output Branch
);

  wire and_1_out;

  and and_1 (and_1_out, CondBranch, ItemIsZero);
  or or_1 (Branch, UncondBranch, and_1_out);

  // Notes on the sheet:
  //   This determines whether we execute a branch.
  //   You can either branch if it's unconditional
  //   OR: It's conditional and you output zero
  //   You see this in BRANCH_IF_ZERO and BRANCH_IF_NOT_ZERO
endmodule

module EightBitZeroChecker (
  input  [7:0] CheckInput,
  output IsAllZero
);

  wire or_1_out;

  or or_1 (or_1_out, CheckInput[0], CheckInput[1], CheckInput[2], CheckInput[3], CheckInput[4], CheckInput[5], CheckInput[6], CheckInput[7]);
  not not_1 (IsAllZero, or_1_out);

  // Notes on the sheet:
  //   Checks if all 8 bits are 0
  //   Notting them will then make it 0
  //   Logic is that if any of these are 1s, the OR gate will return 1.
  //   So the only way this returns 0 is if all 8 bits are 0.
endmodule

module ProgramCounter (
  input  [7:0] NewPC,
  input  ClockTick,
  output [7:0] CurrentPC
);

  Register register_1 (.D(NewPC), .en(1'b1), .clk(ClockTick), .Q(CurrentPC), .clr(1'b0));
endmodule

module WriteRegParser (
  input  WR_As_RR2,
  input  [63:0] BinInstruction,
  output [7:0] WriteReg
);

  Multiplexer #(.width(8)) multiplexer_1 (.in0(BinInstruction[7:0]), .in1({8{1'b0}}), .out(WriteReg), .sel(WR_As_RR2));

  // Notes on the sheet:
  //   LSB
  //   Normally, read from 7 - 0
  //   This is a don't care, but we just return zero
  //   But if WR is now RR2, there is no registers to read from.
endmodule

module IMMParser (
  input  [63:0] BinInstruction,
  output [7:0] IMM
);


  assign IMM = BinInstruction[23:16];

  // Notes on the sheet:
  //   LSB
  //   IMM is always from 23-16
  //   Can be gibberish
  //   If there's no IMM, we don't care this and the output
endmodule

module RD2_Or_Imm_Selector (
  input  [7:0] ReadData2,
  input  [7:0] IMM,
  input  UseImm,
  output [7:0] Value2
);

  Multiplexer #(.width(8)) multiplexer_1 (.in0(ReadData2), .in1(IMM), .out(Value2), .sel(UseImm));

  // Notes on the sheet:
  //   This selects whether we use IMM or ReadData2
endmodule

module WriteDataSelector (
  input  [7:0] ALUOutput,
  input  WriteRegALU,
  input  [7:0] MemOutput,
  input  WriteRegMemory,
  input  [7:0] PC,
  input  PCToX30,
  output [7:0] WriteData
);

  wire [7:0] eightbitadder_1_sum, multiplexer_1_out, multiplexer_2_out;

  Multiplexer #(.width(8)) multiplexer_1 (.in0({8{1'b0}}), .in1(ALUOutput), .out(multiplexer_1_out), .sel(WriteRegALU));
  Multiplexer #(.width(8)) multiplexer_2 (
    .in0(multiplexer_1_out), .in1(MemOutput), .out(multiplexer_2_out), .sel(WriteRegMemory));
  EightBitAdder eightbitadder_1 (.Cin(1'b0), .InputA(8'h8), .InputB(PC), .Sum(eightbitadder_1_sum));  // open: Carry
  Multiplexer #(.width(8)) multiplexer_3 (
    .in0(multiplexer_2_out), .in1(eightbitadder_1_sum), .out(WriteData), .sel(PCToX30));

  // Notes on the sheet:
  //   0 by default
  //   This selects what to write back to WR
  //   But it writes ALU output if that's on
  //   Add PC + 8 if PCToX30 is true
  //   It's writes the item retrieved from memory if that flag's on
endmodule
